// Logisim project Adder1.circ as structural Verilog: 1 circuit, main circuit adder1
module adder1 (
  input  carryIn,
  input  x,
  input  y,
  output sum,
  output carryOut
);

  wire and_1_out, and_2_out, xor_1_out;

  and and_1 (and_1_out, x, y);
  xor xor_1 (xor_1_out, x, y);
  or or_1 (carryOut, and_1_out, and_2_out);
  and and_2 (and_2_out, carryIn, xor_1_out);
  xor xor_2 (sum, carryIn, xor_1_out);
endmodule
