// Logisim project Alu1.circ as structural Verilog: 1 circuit, main circuit alu1
module alu1 (
  input  a,
  input  b,
  input  carryIn,
  input  [1:0] control,
  output carryOut,
  output result
);

  wire adder1_1_carryout, adder1_1_sum, adder1_2_carryout, adder1_2_sum, and_1_out, not_1_out, or_1_out;

  not not_1 (not_1_out, b);
  and and_1 (and_1_out, a, b);
  or or_1 (or_1_out, a, b);
  adder1 adder1_1 (.carryIn(carryIn), .x(a), .y(b), .sum(adder1_1_sum), .carryOut(adder1_1_carryout));
  adder1 adder1_2 (.carryIn(carryIn), .x(a), .y(not_1_out), .sum(adder1_2_sum), .carryOut(adder1_2_carryout));
  Multiplexer #(.select(2), .enable("false")) multiplexer_1 (
    .in0(and_1_out), .in1(or_1_out), .in2(adder1_1_sum), .in3(adder1_2_sum), .out(result), .sel(control));
  Multiplexer #(.select(2), .enable("false")) multiplexer_2 (
    .in0(1'b0), .in1(1'b0), .in2(adder1_1_carryout), .in3(adder1_2_carryout), .out(carryOut), .sel(control));

  // Notes on the sheet:
  //   AND
  //   OR
  //   ADD
  //   SUBTRACT
endmodule
